// Logisim project cpu.circ as structural Verilog: 1 circuit, main circuit cpu
module cpu (
  input  clk,
  input  [31:0] Instruction,
  input  [31:0] MemReadData,
  output [31:0] MemAddress,
  output [31:0] ProgramCounter,
  output [31:0] ra,
  output [31:0] sp,
  output [31:0] t0,
  output [31:0] t1,
  output [31:0] t2,
  output [31:0] s0,
  output [31:0] s1,
  output [31:0] a0,
  output [3:0] MemWriteMask,
  output [31:0] MemWriteData
);

  wire imm7, imm20, memWEn;
  wire [2:0] funct3, immSel;
  wire [3:0] ALUSel, imm30_21;
  wire [4:1] imm11_7;
  wire [6:0] funct7, instr;
  wire [7:3] imm19_12;
  wire [31:0] A, adder_1_out, B, RegWriteData;

  Register #(.width(32)) PC (.D(adder_1_out), .clk(clk), .Q(ProgramCounter));  // open: en, clr
  Adder #(.width(32)) adder_1 (.a(ProgramCounter), .b(32'h4), .out(adder_1_out));  // open: cin, cout
  control_logic control_logic_1 (
    .ImmSel(immSel), .ALUSel(ALUSel), .MemWEn(memWEn),
    .Instruction({funct7, imm30_21, imm20, imm19_12, funct3, imm11_7, imm7, instr}));  // open: PCSel, RegWEn, BrUn, ASel, BSel, WBSel, BrEq, BrLt
  regfile regfile_1 (
    .RegWriteData(RegWriteData), .RegWEn(1'b1), .clk(clk), .ra(ra), .sp(sp), .t0(t0), .t1(t1), .t2(t2),
    .s0(s0), .s1(s1), .a0(a0), .RegReadData1(A), .RegReadData2(B));  // open: ReadReg1, ReadReg2, WriteReg
  imm_gen imm_gen_1 (
    .Instruction({funct7, imm30_21, imm20, imm19_12, funct3, imm11_7, imm7, instr}), .ImmSel(immSel));  // open: Immediate
  Multiplexer #(.enable("false"), .select(5), .width(5)) multiplexer_1 (.sel(instr[6:2]));  // open: in0, in1, in2, in3, in4, in5, in6, in7, in8, in9, in10, in11, in12, in13, in14, in15, in16, in17, in18, in19, in20, in21, in22, in23, in24, in25, in26, in27, in28, in29, in30, in31, out
  alu alu_1 (.ALUResult(RegWriteData), .A(A), .B(B), .ALUSel(ALUSel));
  // branch_comp branch_comp_1: pin names not known
  partial_store partial_store_1 (
    .Instruction({funct7, imm30_21, imm20, imm19_12, funct3, imm11_7, imm7, instr}), .MemAddress(MemAddress),
    .MemWEn(memWEn), .MemWriteMask(MemWriteMask));  // open: DataFromReg, DataToMem
  partial_load partial_load_1 (
    .Instruction({funct7, imm30_21, imm20, imm19_12, funct3, imm11_7, imm7, instr}), .MemAddress(MemAddress));  // open: DataFromMem, DataToReg

  // Other names for the same wires on the sheet: imm19_12[2:0] = funct3;
  //   imm31_12[10:0] = {funct7, imm30_21[3:1], funct3[0]};
  //   instr[31:7] = {funct7, imm30_21, imm20, imm19_12, funct3, imm11_7, imm7};
  //   imm31_20[11:0] = {funct7, imm30_21, imm20}; rs2[4:0] = {imm30_21, imm20}; imm30_21[9:4] = funct7[5:0];
  //   imm30_25[5:0] = funct7[5:0]; imm31_25[6:0] = funct7; imm31 = funct7[6]; imm11_7[0] = imm7;
  //   rd[4:0] = {imm11_7, imm7}; imm11_8[3:0] = imm11_7; rs1[4:0] = imm19_12

  // Notes on the sheet:
  //   To IMEM
  //   IMEM (do **NOT** move this)
  //   From IMEM
  //   rs1
  //   rs2 or imm
  //   rd
  //   opcode
  //   funct3 (might have a problem being undefined)
  //   Inputs/Outputs for testing. Do **NOT** move these.
  //   It is OK to move the PC, RegFile, ALU, MEM, Branch Comp, Imm Gen, Partial Load, Partial Store and Control Logic to wherever is most convenient for you when constructing your CPU, and to delete this text
  //   To DMEM
  //   DMEM (do **NOT** move this)
  //   From DMEM
endmodule
